# Fritzing sketch attiny_rc_switch (saved by Fritzing 0.9.2b)
breadboards: 1

parts:
  U1 = attiny85 [package=dip]
  R1 = Resistor [tolerance=±5% resistance=4.7k package=THT]
  Q1 = NPN-Transistor [part_number=BD139 package="TO92 [THT]"]

nets:
  N1: U1.Pin_2, R1.Pin_1
  GND: U1.Pin_4, Q1.E, Q1.C
  Signal: U1.Pin_5
  +5V: U1.Pin_8
  N2: R1.Pin_0, Q1.B

notes:
  RC receiver
  LiPo Battery
  output
